# Fritzing sketch schematic (saved by Fritzing 0.9.10b)
stripboards: 1

parts:
  Part1 = Adafruit ESP32 Feather V2  # not connected
  Part2 = Adafruit DC+Stepper FeatherWing [part_number="Adafruit #2927"]
  J1 = 2.1mm Barrel Jack with Terminal Block
  C1 = Capacitor Polarized [package=nippon_f80]
  NEOPIXEL1 = Neopixel Strip -- Black (30/m)
  M1 = DC Motor [voltage_(max)=6V voltage_(min)=3V]
  V1 = DC Power [voltage=5]
  S1 = Momentary Switch [package=ksa_sealed_tac_switch]
  S2 = Momentary Switch [package=ksa_sealed_tac_switch]

nets:
  N1: Part2.USB, Part2.VMOTOR, J1.POS, C1.+, NEOPIXEL1.+5V, V1.V+
  N2: Part2.N, NEOPIXEL1.Din
  N3: Part2.J, S1.2
  N4: Part2.H, S2.2
  GND: Part2.GND, J1.NEG, C1.-, NEOPIXEL1.GND, V1.V-, S1.4, S2.4
  N5: Part2.M1A, M1.pin_2

notes:
  Marble Counting Sensor
  Stacked

custom parts:
  Adafruit DC+Stepper FeatherWing: This is the DC Motor + Stepper FeatherWing which will let you use 2 x bi-polar stepper motors or 4 x brushed DC motorx (or 1 stepper and 2 DC motors). Using our Feather Stacking Headers or Feather Female Headers you can connect a FeatherWing on top or bottom of your Feather board and let the board take flight! The original Adafruit Motorshield Kit is one of our most beloved kits, which is why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
  Neopixel Strip -- Black (30/m): These NeoPixel strips have 30 digitally-addressable pixel LEDs per meter and are very affordable and are only 12.5 mm wide, 10 mm if you remove the strip from the casing.
