# Fritzing sketch schematic (saved by Fritzing 0.9.10b)
stripboards: 1

parts:
  Part1 = Adafruit ESP32 Feather V2
  Part2 = Adafruit DC+Stepper FeatherWing [part_number="Adafruit #2927"]
  J1 = 2.1mm Barrel Jack with Terminal Block
  C1 = Capacitor Polarized [package=nippon_f80]
  NEOPIXEL1 = Neopixel Strip -- Black (30/m)  # not connected
  J2 = JST XH 2A male [form="♂ (male)" package=THT]  # not connected
  M1 = DC Motor [voltage_(max)=6V voltage_(min)=3V]  # not connected

nets:
  N1: Part1.I37, Part2.G
  N2: Part1.RX/IO8, Part2.TX
  N3: Part1.TX/IO7, Part2.RX
  N4: Part1.MISO, Part2.MISO
  N5: Part1.MOSI, Part2.MOSI
  N6: Part1.SCK, Part2.SCK
  N7: Part1.A5_IO4, Part2.F
  N8: Part1.A4_I36, Part2.E
  N9: Part1.A3_I39, Part2.D
  N10: Part1.A2_I34, Part2.C
  N11: Part1.A1_DAC1, Part2.B
  N12: Part1.A0_DAC2, Part2.A
  GND: Part1.GND, Part2.GND, J1.NEG, C1.-
  3.3V: Part1.3.3V, Part2.+3.3V
  N13: Part1.!RESET, Part2.RESET
  N14: Part1.VBAT, Part2.VBAT
  N15: Part1.EN, Part2.EN
  N16: Part1.VBUS, Part2.USB, J1.POS, C1.+
  N17: Part1.IO13_A12, Part2.N
  N18: Part1.IO12_A11, Part2.M
  N19: Part1.IO27_A10, Part2.L
  N20: Part1.IO33_A9, Part2.K
  N21: Part1.IO15_A8, Part2.J
  N22: Part1.IO32_A7, Part2.I
  N23: Part1.IO14_A6, Part2.H
  N24: Part1.SCL, Part2.SCL
  N25: Part1.SDA, Part2.SDA

custom parts:
  Adafruit DC+Stepper FeatherWing: This is the DC Motor + Stepper FeatherWing which will let you use 2 x bi-polar stepper motors or 4 x brushed DC motorx (or 1 stepper and 2 DC motors). Using our Feather Stacking Headers or Feather Female Headers you can connect a FeatherWing on top or bottom of your Feather board and let the board take flight! The original Adafruit Motorshield Kit is one of our most beloved kits, which is why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
  Neopixel Strip -- Black (30/m): These NeoPixel strips have 30 digitally-addressable pixel LEDs per meter and are very affordable and are only 12.5 mm wide, 10 mm if you remove the strip from the casing.
  JST XH 2A male: JST XH-2A
